# Fritzing sketch hwdiagram (saved by Fritzing 0.9.6b)
breadboards: 1

parts:
  WeMos_D1_Mini_WS2812B_RGB_Shield1 = WeMos D1 Mini WS2812B RGB Shield
  LED1 = LED - 5mm [color="Red (633nm)" package="5 mm [THT]"]
  R1 = Resistor [tolerance=±5% resistance=220 package=THT]
  R2 = Resistor [tolerance=±5% resistance=220 package=THT]
  R3 = Resistor [tolerance=±5% resistance=220 package=THT]
  LED2 = LED - 5mm [color="Orange (605nm)" package="5 mm [THT]"]
  LED3 = LED - 5mm [color="Green (555nm)" package="5 mm [THT]"]
  LED4 = LED - 5mm [color="Orange (605nm)" package="5 mm [THT]"]
  LED5 = LED - 5mm [color="Red (633nm)" package="5 mm [THT]"]
  LED6 = LED - 5mm [color="Green (555nm)" package="5 mm [THT]"]
  R4 = Resistor [tolerance=±5% resistance=220 package=THT]
  R5 = Resistor [tolerance=±5% resistance=220 package=THT]
  R6 = Resistor [tolerance=±5% resistance=220 package=THT]
  S1 = Pushbutton [package="[THT]"]
  WeMos_D1_Mini1 = WeMos D1 Mini
  S2 = Pushbutton [package="[THT]"]
  R7 = Resistor [tolerance=±5% resistance=220 package=THT]
  R8 = Resistor [tolerance=±5% resistance=220 package=THT]

nets:
  N1: WeMos_D1_Mini_WS2812B_RGB_Shield1.3V3, R1.Pin_0, R2.Pin_0, R3.Pin_0, R4.Pin_0, R5.Pin_0, R6.Pin_0, R7.Pin_0, R8.Pin_0
  N2: WeMos_D1_Mini_WS2812B_RGB_Shield1.D1, LED1.cathode
  N3: WeMos_D1_Mini_WS2812B_RGB_Shield1.D2, LED2.cathode
  N4: WeMos_D1_Mini_WS2812B_RGB_Shield1.D5, S1.Pin_1, S1.Pin_2, R8.Pin_1
  N5: WeMos_D1_Mini_WS2812B_RGB_Shield1.D6, LED6.cathode
  N6: WeMos_D1_Mini_WS2812B_RGB_Shield1.D7, LED4.cathode
  N7: WeMos_D1_Mini_WS2812B_RGB_Shield1.D8, LED5.cathode
  N8: LED1.anode, R1.Pin_1
  N9: R2.Pin_1, LED2.anode
  N10: R3.Pin_1, LED3.anode
  N11: LED3.cathode, WeMos_D1_Mini1.D3
  N12: LED4.anode, R4.Pin_1
  N13: LED5.anode, R6.Pin_1
  N14: LED6.anode, R5.Pin_1
  N15: S1.Pin_3, S1.Pin_4, WeMos_D1_Mini1.G, S2.Pin_1, S2.Pin_2
  N16: WeMos_D1_Mini1.D4, S2.Pin_3, S2.Pin_4, R7.Pin_1
